# Fritzing sketch wipi (saved by Fritzing 0.9.9b)
circuit board: 6.65cm x 5.79cm
breadboards: 1

parts:
  74LVC245_(CB1-CB2) = 74LVC245 Octal 2-Way Tranceiver [part_number=74LVC245]
  74LVC245_(PB0-PB7) = 74LVC245 Octal 2-Way Tranceiver [part_number=74LVC245]
  Userport = male pin header, 10 pins [form="♂ (male)"]
  1 = male pin header, 10 pins [form="♂ (male)"]
  Ext_Power = rounded female pin header, 2 pins [form="♀ (female rounded)"]
  D1 = Schottky Diode [part_number=1N5817 package="300 mil [THT]"]
  21-40 = rounded female pin header, 20 pins [form="♀ (female rounded)"]
  1-20 = rounded female pin header, 20 pins [form="♀ (female rounded)"]
  Int_5v_Ext_5v = Toggle Switch [package=THT]
  C1 = Capacitor [package=cap-pth-small2]
  C2 = Capacitor [package=cap-pth-small2]

nets:
  VCC: 74LVC245_(CB1-CB2).DIR, 74LVC245_(CB1-CB2).VCC, 74LVC245_(PB0-PB7).VCC, 21-40.pin5, C1.1, C2.1
  N1: 74LVC245_(CB1-CB2).A7, 1-20.pin12
  GND: 74LVC245_(CB1-CB2).GND, 74LVC245_(CB1-CB2).!OE, 74LVC245_(PB0-PB7).GND, 74LVC245_(PB0-PB7).!OE, Userport.pin1, Userport.pin2, Userport.pin3, Userport.pin4, Userport.pin5, Userport.pin6, Userport.pin7, Userport.pin8, Ext_Power.pin1, 21-40.pin3, 21-40.pin8, 21-40.pin13, 21-40.pin18, 1-20.pin3, 1-20.pin8, 1-20.pin13, 1-20.pin18, C1.2, C2.2
  N2: 74LVC245_(CB1-CB2).A8, 1.pin9
  N3: 74LVC245_(CB1-CB2).B8, 1-20.pin11
  N4: 74LVC245_(CB1-CB2).B7, 1.pin10
  N5: 74LVC245_(PB0-PB7).DIR, 1-20.pin14
  N6: 74LVC245_(PB0-PB7).A1, 1.pin8
  N7: 74LVC245_(PB0-PB7).A2, 1.pin7
  N8: 74LVC245_(PB0-PB7).A3, 1.pin6
  N9: 74LVC245_(PB0-PB7).A4, 1.pin5
  N10: 74LVC245_(PB0-PB7).A5, 1.pin4
  N11: 74LVC245_(PB0-PB7).A6, 1.pin3
  N12: 74LVC245_(PB0-PB7).A7, 1.pin2
  N13: 74LVC245_(PB0-PB7).A8, 1.pin1
  N14: 74LVC245_(PB0-PB7).B8, 1-20.pin10
  N15: 74LVC245_(PB0-PB7).B7, 1-20.pin9
  N16: 74LVC245_(PB0-PB7).B6, 1-20.pin7
  N17: 74LVC245_(PB0-PB7).B5, 1-20.pin6
  N18: 74LVC245_(PB0-PB7).B4, 1-20.pin5
  N19: 74LVC245_(PB0-PB7).B3, 1-20.pin4
  N20: 74LVC245_(PB0-PB7).B2, 1-20.pin2
  N21: 74LVC245_(PB0-PB7).B1, 1-20.pin1
  N22: Userport.pin9, Userport.pin10, Int_5v_Ext_5v.L2
  N23: Ext_Power.pin2, Int_5v_Ext_5v.L1
  N24: D1.cathode, 21-40.pin2
  N25: D1.anode, Int_5v_Ext_5v.COM

notes:
  Revision 2 : 06042024
  WiPi : Wireless Network Adaptor
  +   -
  Pi Pico W
  USB

custom parts:
  74LVC245 Octal 2-Way Tranceiver: 74LVC245 Octal Bi-directional Tri-state Transceiver
