# Fritzing sketch wipi_v2 (saved by Fritzing 0.9.9b)
circuit board: 6.48064cm x 4.99099cm
breadboards: 1

parts:
  IC1 = 74LVC245 Octal 2-Way Tranceiver [part_number=74LVC245]
  J2 = male pin header, 10 pins [form="♂ (male)"]
  J4 = rounded female pin header, 20 pins [form="♀ (female rounded)"]
  J5 = rounded female pin header, 2 pins [form="♀ (female rounded)"]
  D1 = Schottky Diode [part_number=1N5817 package="300 mil [THT]"]
  S1 = Toggle Switch [package=THT]
  J3 = rounded female pin header, 20 pins [form="♀ (female rounded)"]
  IC2 = 74LVC245 Octal 2-Way Tranceiver [part_number=74LVC245]
  J6 = male pin header, 10 pins [form="♂ (male)"]  # not connected

nets:
  GND: IC1.DIR, IC1.GND, IC1.!OE, J4.pin3, J4.pin8, J4.pin13, J4.pin18, J5.pin1, J3.pin3, J3.pin8, J3.pin13, J3.pin18, IC2.GND, IC2.!OE
  N1: IC1.A7, J4.pin12
  N2: IC1.B8, J4.pin11
  VCC: IC1.VCC, J3.pin5, IC2.VCC
  N3: J2.pin9, J2.pin10
  N4: J4.pin1, IC2.B8
  N5: J4.pin2, IC2.B7
  N6: J4.pin4, IC2.B6
  N7: J4.pin5, IC2.B5
  N8: J4.pin6, IC2.B4
  N9: J4.pin7, IC2.B3
  N10: J4.pin9, IC2.B2
  N11: J4.pin10, IC2.B1
  N12: J4.pin14, IC2.DIR
  N13: J5.pin2, S1.L1
  N14: D1.cathode, J3.pin2
  N15: D1.anode, S1.COM

custom parts:
  74LVC245 Octal 2-Way Tranceiver: 74LVC245 Octal Bi-directional Tri-state Transceiver
